# Fritzing sketch nail2nail (saved by Fritzing 0.9.0b)
breadboards: 1

parts:
  Part1 = Arduino Uno (Rev3)
  R1 = Resistor [tolerance=±5% resistance=220 package=THT]
  ANT1 = Antenna  # not connected
  ANT2 = Antenna

nets:
  N1: Part1.A0, R1.Pin_0
  N2: Part1.D2, R1.Pin_1
  N3: Part1.D3_PWM, ANT2.antenna_lead
